// Logisim project ProjectDigitalDesign.circ as structural Verilog: 10 circuits, main circuit DigitalDisplay
module main (
  input  E,
  input  X,
  input  R
);

  wire CLK_out, controller_1_e0, controller_1_e1, controller_1_x0, controller_1_x1, lightselector_1_green,
       lightselector_1_red, lightselector_1_yellow, lightselector_2_green, lightselector_2_red,
       lightselector_2_yellow;
  wire [3:0] controller_1_c;

  Clock #(.highDuration(5)) CLK (.out(CLK_out));
  Controller controller_1 (
    .E(E), .X(X), .CLK(CLK_out), .R(R), .E0(controller_1_e0), .E1(controller_1_e1), .X0(controller_1_x0),
    .X1(controller_1_x1), .C(controller_1_c));
  DigitalDisplay digitaldisplay_1 (.in_1(controller_1_c));
  LightSelector lightselector_1 (
    .L_0(controller_1_e0), .L_1(controller_1_e1), .Red(lightselector_1_red), .Yellow(lightselector_1_yellow),
    .Green(lightselector_1_green));
  LightSelector lightselector_2 (
    .L_0(controller_1_x0), .L_1(controller_1_x1), .Red(lightselector_2_red), .Yellow(lightselector_2_yellow),
    .Green(lightselector_2_green));
  LED led_1 (.in(lightselector_1_red));
  LED led_2 (.in(lightselector_1_yellow));
  LED led_3 (.in(lightselector_1_green));
  LED led_4 (.in(lightselector_2_red));
  LED led_5 (.in(lightselector_2_yellow));
  LED led_6 (.in(lightselector_2_green));

  // Notes on the sheet:
  //   Entrance
  //   Exit
endmodule

module DigitalDisplay (
  input  [3:0] in_1
);

  wire and_1_out, and_2_out, and_3_out, and_4_out, and_5_out, and_6_out, and_7_out, and_8_out, and_9_out,
       and_10_out, and_11_out, and_12_out, and_13_out, and_14_out, and_15_out, and_16_out, and_17_out,
       and_18_out, and_19_out, and_20_out, and_21_out, and_22_out, and_23_out, and_24_out, and_25_out,
       and_26_out, not_1_out, not_2_out, not_3_out, not_4_out, or_1_out, or_2_out, or_3_out, or_4_out,
       or_5_out, or_6_out, or_7_out;

  not not_1 (not_1_out, in_1[3]);
  not not_2 (not_2_out, in_1[2]);
  not not_3 (not_3_out, in_1[1]);
  not not_4 (not_4_out, in_1[0]);
  and and_1 (and_1_out, not_1_out, in_1[1]);
  and and_2 (and_2_out, not_1_out, in_1[2], in_1[0]);
  and and_3 (and_3_out, in_1[3], not_2_out, not_3_out);
  and and_4 (and_4_out, not_2_out, not_3_out, not_4_out);
  and and_5 (and_5_out, not_1_out, not_2_out);
  and and_6 (and_6_out, not_2_out, not_3_out);
  and and_7 (and_7_out, not_1_out, in_1[1], in_1[0]);
  and and_8 (and_8_out, not_1_out, not_3_out, not_4_out);
  and and_9 (and_9_out, not_1_out, in_1[2]);
  and and_10 (and_10_out, not_2_out, not_3_out);
  and and_11 (and_11_out, not_1_out, in_1[0]);
  and and_12 (and_12_out, not_4_out, not_3_out, not_2_out);
  and and_13 (and_13_out, in_1[3], not_2_out, not_3_out);
  and and_14 (and_14_out, not_1_out, not_2_out, in_1[1]);
  and and_15 (and_15_out, in_1[1], not_4_out, not_1_out);
  and and_16 (and_16_out, not_1_out, in_1[2], not_3_out, in_1[0]);
  and and_17 (and_17_out, not_3_out, not_4_out, not_2_out);
  and and_18 (and_18_out, in_1[1], not_4_out, not_1_out);
  and and_19 (and_19_out, not_3_out, not_4_out, not_1_out);
  and and_20 (and_20_out, not_1_out, in_1[2], not_3_out);
  and and_21 (and_21_out, not_1_out, in_1[2], not_4_out);
  and and_22 (and_22_out, in_1[3], not_2_out, not_3_out);
  and and_23 (and_23_out, not_1_out, not_2_out, in_1[1]);
  and and_24 (and_24_out, not_1_out, in_1[2], not_3_out);
  and and_25 (and_25_out, in_1[2], not_4_out, not_1_out);
  and and_26 (and_26_out, in_1[3], not_2_out, not_3_out);
  or or_1 (or_1_out, and_17_out, and_18_out);
  or or_2 (or_2_out, and_19_out, and_20_out, and_21_out, and_22_out);
  or or_3 (or_3_out, and_23_out, and_24_out, and_25_out, and_26_out);
  or or_4 (or_4_out, and_1_out, and_2_out, and_3_out, and_4_out);
  or or_5 (or_5_out, and_5_out, and_6_out, and_7_out, and_8_out);
  or or_6 (or_6_out, and_9_out, and_10_out, and_11_out);
  or or_7 (or_7_out, and_12_out, and_13_out, and_14_out, and_15_out, and_16_out);
  _7_Segment_Display Display (
    .g(or_3_out), .f(or_2_out), .a(or_4_out), .b(or_5_out), .e(or_1_out), .d(or_7_out), .c(or_6_out));  // open: dp
endmodule

module SRLatch (
  input  R,
  input  S,
  output Q,
  output out_4
);

  nor nor_1 (Q, R, out_4);
  nor nor_2 (out_4, Q, S);
endmodule

module DLatch (
  input  CLK,
  input  D,
  output Q,
  output out_4
);

  wire and_1_out, and_2_out, not_1_out;

  not not_1 (not_1_out, D);
  and and_1 (and_1_out, CLK, not_1_out);
  and and_2 (and_2_out, CLK, D);
  SRLatch srlatch_1 (.out_4(out_4), .Q(Q), .S(and_2_out), .R(and_1_out));
endmodule

module DFlipFlop (
  input  CLK,
  input  D,
  output Q,
  output out_4
);

  wire dlatch_1_q, not_1_out;

  not not_1 (not_1_out, CLK);
  DLatch dlatch_1 (.Q(dlatch_1_q), .D(D), .CLK(not_1_out));  // open: out_4
  DLatch dlatch_2 (.out_4(out_4), .Q(Q), .D(dlatch_1_q), .CLK(CLK));
endmodule

module LightSelector (
  input  L_0,
  input  L_1,
  output Red,
  output Yellow,
  output Green
);

  wire not_1_out, not_2_out;

  not not_1 (not_1_out, L_0);
  not not_2 (not_2_out, L_1);
  and and_1 (Red, L_0, not_2_out);
  and and_2 (Yellow, not_1_out, L_1);
  and and_3 (Green, not_2_out, not_1_out);
endmodule

module SettableFlipFlop (
  input  CLK,
  input  D,
  input  S,
  output Q
);

  wire or_1_out;

  or or_1 (or_1_out, D, S);
  DFlipFlop dflipflop_1 (.Q(Q), .CLK(CLK), .D(or_1_out));  // open: out_4
endmodule

module Controller (
  input  E,
  input  X,
  input  CLK,
  input  R,
  output E0,
  output E1,
  output X0,
  output X1,
  output [3:0] C
);

  wire [5:0] register_1_q, transitiontable_1_n1;

  TransitionTable transitiontable_1 (
    .S1(register_1_q[0]), .S2(register_1_q[1]), .S3(register_1_q[2]), .S4(register_1_q[3]),
    .S5(register_1_q[4]), .S6(register_1_q[5]), .E(E), .X(X), .N1(transitiontable_1_n1[0]),
    .N2(transitiontable_1_n1[1]), .N3(transitiontable_1_n1[2]), .N4(transitiontable_1_n1[3]),
    .N5(transitiontable_1_n1[4]), .N6(transitiontable_1_n1[5]));
  Register #(.width(6)) register_1 (.D(transitiontable_1_n1), .clk(CLK), .Q(register_1_q), .clr(R));  // open: en
  ActionTable actiontable_1 (
    .S1(register_1_q[0]), .S2(register_1_q[1]), .S3(register_1_q[2]), .S4(register_1_q[3]),
    .S5(register_1_q[4]), .S6(register_1_q[5]), .C1(C[3]), .C2(C[2]), .C3(C[1]), .C4(C[0]), .E0(E0), .E1(E1),
    .X0(X0), .X1(X1));

  // Notes on the sheet:
  //   S1
  //   S2
  //   S3
  //   S6
  //   S4
  //   S5
endmodule

module ActionTable (
  input  S1,
  input  S2,
  input  S3,
  input  S4,
  input  S5,
  input  S6,
  output C1,
  output C2,
  output C3,
  output C4,
  output E0,
  output E1,
  output X0,
  output X1
);

  wire and_1_out, and_2_out, and_3_out, and_4_out, and_5_out, and_6_out, and_7_out, and_8_out, and_9_out,
       and_10_out, and_11_out, and_12_out, and_13_out, and_14_out, and_15_out, and_16_out, and_17_out,
       and_18_out, and_19_out, and_20_out, and_21_out, and_22_out, and_23_out, and_24_out, and_25_out,
       and_26_out, and_27_out, and_28_out, and_29_out, and_30_out, and_31_out, and_32_out, and_33_out,
       and_34_out, and_35_out, and_36_out, and_37_out, and_38_out, and_39_out, and_40_out, and_41_out,
       and_42_out, not_1_out, not_2_out, not_3_out, not_4_out, not_5_out, not_6_out;

  not not_1 (not_1_out, S1);
  not not_2 (not_2_out, S2);
  not not_3 (not_3_out, S3);
  not not_4 (not_4_out, S4);
  not not_5 (not_5_out, S5);
  not not_6 (not_6_out, S6);
  and and_1 (and_1_out, not_2_out, S3, not_4_out, not_5_out);
  and and_2 (and_2_out, S1, S4, S5, S6);
  and and_3 (and_3_out, S1, S3);
  and and_4 (and_4_out, not_1_out, not_2_out, not_3_out, S4);
  and and_5 (and_5_out, not_1_out, not_3_out, S4, S5, S6);
  and and_6 (and_6_out, S2, S3);
  and and_7 (and_7_out, S1, not_3_out, not_4_out);
  and and_8 (and_8_out, S1, not_3_out, not_6_out);
  and and_9 (and_9_out, S1, S4, not_5_out, S6);
  and and_10 (and_10_out, not_1_out, not_2_out, not_3_out, S5);
  and and_11 (and_11_out, not_3_out, not_4_out, S5);
  and and_12 (and_12_out, S3, S4, S5, S6);
  and and_13 (and_13_out, S2, not_3_out, not_5_out);
  and and_14 (and_14_out, S2, not_3_out, not_6_out);
  and and_15 (and_15_out, S1, not_3_out, not_5_out);
  and and_16 (and_16_out, S1, not_3_out, not_6_out);
  and and_17 (and_17_out, not_1_out, not_2_out, not_3_out, S6);
  and and_18 (and_18_out, not_1_out, not_2_out, not_5_out, S6);
  and and_19 (and_19_out, not_4_out, S5, S6);
  and and_20 (and_20_out, S4, not_5_out, S6);
  and and_21 (and_21_out, S3, S4, not_6_out);
  and and_22 (and_22_out, S2, S4, not_6_out);
  and and_23 (and_23_out, S1, S4, not_6_out);
  and and_24 (and_24_out, S1, S3, S4);
  and and_25 (and_25_out, not_1_out, not_2_out, S3, not_4_out, S5, not_6_out);
  and and_26 (and_26_out, S3, S4, not_5_out);
  and and_27 (and_27_out, S2, not_5_out);
  and and_28 (and_28_out, S1, not_5_out);
  and and_29 (and_29_out, S3, S5, S6);
  and and_30 (and_30_out, S2, S5, S6);
  and and_31 (and_31_out, S1, S5, S6);
  and and_32 (and_32_out, not_1_out, not_2_out, not_3_out);
  and and_33 (and_33_out, not_1_out, not_2_out, not_4_out, not_5_out);
  and and_34 (and_34_out, not_1_out, not_2_out, not_4_out, S6);
  and and_35 (and_35_out, S5, S6);
  and and_36 (and_36_out, S4, S5);
  and and_37 (and_37_out, S2, S5);
  and and_38 (and_38_out, S1, S5);
  and and_39 (and_39_out, not_1_out, not_2_out, S3, not_4_out, S5, not_6_out);
  and and_40 (and_40_out, S3, S4, not_5_out, S6);
  and and_41 (and_41_out, S2, not_5_out, S6);
  and and_42 (and_42_out, S1, not_5_out, S6);
  or or_1 (C1, and_1_out, and_2_out, and_3_out);
  or or_2 (E0, and_25_out, and_26_out, and_27_out, and_28_out);
  or or_3 (E1, and_29_out, and_30_out, and_31_out);
  or or_4 (X1, and_39_out, and_40_out, and_41_out, and_42_out);
  or or_5 (C2, and_4_out, and_5_out, and_6_out, and_7_out, and_8_out, and_9_out);
  or or_6 (C3, and_10_out, and_11_out, and_12_out, and_13_out, and_14_out, and_15_out, and_16_out);
  or or_7 (C4, and_17_out, and_18_out, and_19_out, and_20_out, and_21_out, and_22_out, and_23_out, and_24_out);
  or or_8 (X0, and_32_out, and_33_out, and_34_out, and_35_out, and_36_out, and_37_out, and_38_out);
endmodule

module TransitionTable (
  input  S1,
  input  S2,
  input  S3,
  input  S4,
  input  S5,
  input  S6,
  input  E,
  input  X,
  output N1,
  output N2,
  output N3,
  output N4,
  output N5,
  output N6
);

  wire and_1_out, and_2_out, and_3_out, and_4_out, and_5_out, and_6_out, and_7_out, and_8_out, and_9_out,
       and_10_out, and_11_out, and_12_out, and_13_out, and_14_out, and_15_out, and_16_out, and_17_out,
       and_18_out, and_19_out, and_20_out, and_21_out, and_22_out, and_23_out, and_24_out, and_25_out,
       and_26_out, and_27_out, and_28_out, and_29_out, and_30_out, and_31_out, and_32_out, and_33_out,
       and_34_out, and_35_out, and_36_out, and_37_out, and_38_out, and_39_out, and_40_out, and_41_out,
       and_42_out, and_43_out, and_44_out, and_45_out, and_46_out, and_47_out, and_48_out, and_49_out,
       and_50_out, and_51_out, and_52_out, and_53_out, and_54_out, and_55_out, and_56_out, and_57_out,
       and_58_out, and_59_out, and_60_out, and_61_out, and_62_out, and_63_out, and_64_out, and_65_out,
       and_66_out, and_67_out, and_68_out, and_69_out, and_70_out, and_71_out, and_72_out, and_73_out,
       and_74_out, and_75_out, and_76_out, and_77_out, and_78_out, and_79_out, not_1_out, not_2_out,
       not_3_out, not_4_out, not_5_out, not_6_out, not_7_out, not_8_out;

  not not_1 (not_1_out, S1);
  not not_2 (not_2_out, S2);
  not not_3 (not_3_out, S3);
  not not_4 (not_4_out, S4);
  not not_5 (not_5_out, S5);
  not not_6 (not_6_out, S6);
  not not_7 (not_7_out, E);
  not not_8 (not_8_out, X);
  and and_1 (and_1_out, not_2_out, not_3_out, S4, S5, S6, X);
  and and_2 (and_2_out, not_2_out, S3, not_4_out, not_5_out, X);
  and and_3 (and_3_out, S2, not_3_out, S4, not_5_out, not_6_out, E, not_8_out);
  and and_4 (and_4_out, S2, S3, S4, S5, S6);
  and and_5 (and_5_out, S1, not_5_out, not_8_out);
  and and_6 (and_6_out, S1, S6);
  and and_7 (and_7_out, S1, S4, not_5_out);
  and and_8 (and_8_out, not_1_out, not_3_out, not_4_out, S5, S6, X);
  and and_9 (and_9_out, not_1_out, not_2_out, not_3_out, S4, not_6_out, X);
  and and_10 (and_10_out, not_1_out, not_3_out, S4, not_5_out, X);
  and and_11 (and_11_out, not_2_out, S3, S4, S5, S6);
  and and_12 (and_12_out, S2, not_4_out, not_5_out, not_8_out);
  and and_13 (and_13_out, S2, not_5_out, not_7_out, not_8_out);
  and and_14 (and_14_out, S2, not_3_out, S6);
  and and_15 (and_15_out, S2, not_4_out, S6);
  and and_16 (and_16_out, S2, S3, not_5_out);
  and and_17 (and_17_out, S1, not_3_out, not_4_out, not_5_out, not_6_out, X);
  and and_18 (and_18_out, not_1_out, not_2_out, not_5_out, S6, X);
  and and_19 (and_19_out, not_1_out, not_2_out, not_3_out, S5, not_6_out, X);
  and and_20 (and_20_out, not_3_out, S4, S5, S6, E, not_8_out);
  and and_21 (and_21_out, S3, not_5_out, not_8_out);
  and and_22 (and_22_out, S3, not_4_out, S6);
  and and_23 (and_23_out, S3, S4, not_5_out);
  and and_24 (and_24_out, S2, not_3_out, not_4_out, not_5_out, not_6_out, X);
  and and_25 (and_25_out, S2, S4, not_5_out, not_6_out, E, not_8_out);
  and and_26 (and_26_out, S2, not_3_out, S4, S5, S6);
  and and_27 (and_27_out, S1, not_3_out, not_4_out, not_5_out, not_6_out, X);
  and and_28 (and_28_out, S1, S4, S5, E);
  and and_29 (and_29_out, S1, S4, S5, S6);
  and and_30 (and_30_out, S1, S3, S6);
  and and_31 (and_31_out, S1, S3, S5);
  and and_32 (and_32_out, not_1_out, not_2_out, not_3_out, S5, not_6_out, X);
  and and_33 (and_33_out, not_4_out, S5, S6, E, not_8_out);
  and and_34 (and_34_out, not_1_out, not_2_out, not_3_out, S4, not_6_out);
  and and_35 (and_35_out, not_1_out, not_2_out, not_3_out, S4, not_7_out, not_8_out);
  and and_36 (and_36_out, not_2_out, S4, not_5_out, not_8_out);
  and and_37 (and_37_out, S4, not_5_out, not_7_out, not_8_out);
  and and_38 (and_38_out, not_1_out, not_3_out, S4, S5, not_6_out, E);
  and and_39 (and_39_out, S3, not_4_out, not_5_out, not_6_out, X);
  and and_40 (and_40_out, S3, not_4_out, S5, S6);
  and and_41 (and_41_out, S3, S4, not_5_out, not_8_out);
  and and_42 (and_42_out, S3, S4, not_5_out, S6);
  and and_43 (and_43_out, S2, not_4_out, not_5_out, not_6_out, X);
  and and_44 (and_44_out, S2, not_4_out, S5, S6);
  and and_45 (and_45_out, S2, S4, not_5_out, S6);
  and and_46 (and_46_out, S2, S3, S5, not_6_out);
  and and_47 (and_47_out, S1, not_3_out, not_4_out, not_6_out, X);
  and and_48 (and_48_out, S1, not_3_out, not_4_out, S5);
  and and_49 (and_49_out, S1, not_3_out, S5, not_6_out, not_7_out);
  and and_50 (and_50_out, S1, S4, not_5_out, S6);
  and and_51 (and_51_out, not_2_out, not_5_out, S6, X);
  and and_52 (and_52_out, not_2_out, not_3_out, not_5_out, S6, E);
  and and_53 (and_53_out, not_1_out, not_2_out, not_3_out, S5, not_6_out);
  and and_54 (and_54_out, not_1_out, not_2_out, not_3_out, S5, not_7_out);
  and and_55 (and_55_out, not_3_out, not_4_out, S5, not_6_out);
  and and_56 (and_56_out, not_3_out, S5, not_6_out, not_7_out);
  and and_57 (and_57_out, not_1_out, not_2_out, not_3_out, S5, X);
  and and_58 (and_58_out, not_1_out, not_2_out, not_3_out, S4, X);
  and and_59 (and_59_out, not_1_out, not_2_out, S4, not_6_out, E, X);
  and and_60 (and_60_out, not_1_out, not_2_out, S3, not_5_out, X);
  and and_61 (and_61_out, S3, S4, not_5_out, S6);
  and and_62 (and_62_out, S3, S4, S5, not_6_out, E);
  and and_63 (and_63_out, S2, not_4_out, not_5_out, S6);
  and and_64 (and_64_out, S1, not_5_out, S6);
  and and_65 (and_65_out, not_1_out, not_2_out, not_3_out, not_6_out, E);
  and and_66 (and_66_out, not_2_out, not_5_out, not_6_out, E, not_8_out);
  and and_67 (and_67_out, not_3_out, not_4_out, not_6_out, E, not_8_out);
  and and_68 (and_68_out, not_1_out, not_2_out, not_3_out, S6, not_7_out);
  and and_69 (and_69_out, not_1_out, not_2_out, not_3_out, S6, X);
  and and_70 (and_70_out, not_1_out, not_2_out, not_3_out, S5, X);
  and and_71 (and_71_out, not_1_out, not_2_out, not_3_out, S4, X);
  and and_72 (and_72_out, S4, not_5_out, not_6_out, E, not_8_out);
  and and_73 (and_73_out, not_1_out, not_2_out, S3, not_4_out, not_5_out, X);
  and and_74 (and_74_out, not_1_out, not_2_out, S3, not_4_out, not_5_out, S6);
  and and_75 (and_75_out, S3, S4, S5, not_6_out, not_7_out);
  and and_76 (and_76_out, S2, not_4_out, S5, not_6_out, E);
  and and_77 (and_77_out, S2, S4, S5, not_6_out, not_7_out);
  and and_78 (and_78_out, S1, not_4_out, S5, not_6_out, E);
  and and_79 (and_79_out, S1, S4, S5, not_6_out, not_7_out);
  or or_1 (N1, and_1_out, and_2_out, and_3_out, and_4_out, and_5_out, and_6_out, and_7_out);
  or or_2 (N2, and_8_out, and_9_out, and_10_out, and_11_out, and_12_out, and_13_out, and_14_out, and_15_out, and_16_out, and_17_out);
  or or_3 (N3, and_18_out, and_19_out, and_20_out, and_21_out, and_22_out, and_23_out, and_24_out, and_25_out, and_26_out, and_27_out, and_28_out, and_29_out, and_30_out, and_31_out);
  or or_4 (N4, and_32_out, and_33_out, and_34_out, and_35_out, and_36_out, and_37_out, and_38_out, and_39_out, and_40_out, and_41_out, and_42_out, and_43_out, and_44_out, and_45_out, and_46_out, and_47_out, and_48_out, and_49_out, and_50_out);
  or or_5 (N5, and_51_out, and_52_out, and_53_out, and_54_out, and_55_out, and_56_out, and_57_out, and_58_out, and_59_out, and_60_out, and_61_out, and_62_out, and_63_out, and_64_out);
  or or_6 (N6, and_65_out, and_66_out, and_67_out, and_68_out, and_69_out, and_70_out, and_71_out, and_72_out, and_73_out, and_74_out, and_75_out, and_76_out, and_77_out, and_78_out, and_79_out);
endmodule
